// Logisim project hw3.circ as structural Verilog: 3 circuits, main circuit 1-Bit Full Adder
module _1_Bit_Full_Adder (
  input  A,
  input  B,
  input  CarryIn,
  output Answer,
  output CarryOut
);

  wire and_1_out, and_2_out, xor_1_out;

  xor xor_1 (xor_1_out, A, B);
  xor xor_2 (Answer, xor_1_out, CarryIn);
  and and_1 (and_1_out, xor_1_out, CarryIn);
  and and_2 (and_2_out, A, B);
  or or_1 (CarryOut, and_1_out, and_2_out);
endmodule

module _4_Bit_Full_Adder (
  input  CarryIn,
  input  [3:0] A,
  input  [3:0] B,
  output [3:0] Answer,
  output CarryOut
);

  wire _0_carryout, _1_carryout, _2_carryout;

  _1_Bit_Full_Adder _0 (.A(A[0]), .B(B[0]), .CarryIn(CarryIn), .Answer(Answer[0]), .CarryOut(_0_carryout));
  _1_Bit_Full_Adder _1 (.A(A[1]), .B(B[1]), .CarryIn(_0_carryout), .Answer(Answer[1]), .CarryOut(_1_carryout));
  _1_Bit_Full_Adder _2 (.A(A[2]), .B(B[2]), .CarryIn(_1_carryout), .Answer(Answer[2]), .CarryOut(_2_carryout));
  _1_Bit_Full_Adder _3 (.A(A[3]), .B(B[3]), .CarryIn(_2_carryout), .Answer(Answer[3]), .CarryOut(CarryOut));
endmodule

module _4_Bit_ALU (
  input  [3:0] A,
  input  S2,
  input  S1,
  input  S0,
  input  [3:0] B,
  output [3:0] Answer
);

  wire or_2_out;
  wire [0:0] not_1_out;
  wire [3:0] and_1_out, multiplexer_1_out, multiplexer_2_out, n4_bit_full_adder_1_answer, not_2_out,
       not_3_out, or_1_out, xor_1_out;
  wire [3:3] not_4_out;

  not not_1 (not_1_out[0], S1);
  assign not_2_out = ~A;  // NOT_Gate not_2, 4 bits wide
  assign not_3_out = ~B;  // NOT_Gate not_3, 4 bits wide
  not not_4 (not_4_out[3], S1);
  Multiplexer #(.select(2), .width(4), .disabled(0), .enable("false")) multiplexer_1 (
    .in0(A), .in1(A), .in2(A), .in3(not_2_out), .out(multiplexer_1_out), .sel({S1, S0}));
  Multiplexer #(.select(2), .width(4), .disabled(0), .enable("false")) multiplexer_2 (
    .in0(B), .in1(not_3_out), .in2({{3{S1}}, not_1_out[0]}), .in3({4{not_4_out[3]}}),
    .out(multiplexer_2_out), .sel({S1, S0}));
  assign and_1_out = A & B;  // AND_Gate and_1, 4 bits wide
  assign or_1_out = A | B;  // OR_Gate or_1, 4 bits wide
  assign xor_1_out = A ^ B;  // XOR_Gate xor_1, 4 bits wide
  _4_Bit_Full_Adder u_4_bit_full_adder_1 (
    .CarryIn(or_2_out), .A(multiplexer_1_out), .B(multiplexer_2_out), .Answer(n4_bit_full_adder_1_answer));  // open: CarryOut
  or or_2 (or_2_out, S0, S1);
  Multiplexer #(.select(3), .width(4), .disabled(0), .enable("false")) multiplexer_3 (
    .in0(n4_bit_full_adder_1_answer), .in1(n4_bit_full_adder_1_answer), .in2(n4_bit_full_adder_1_answer),
    .in3(n4_bit_full_adder_1_answer), .in4(n4_bit_full_adder_1_answer), .in5(and_1_out), .in6(or_1_out),
    .in7(xor_1_out), .out(Answer), .sel({S2, S1, S0}));

  // Notes on the sheet:
  //   101 AND
  //   110 OR
  //   111 XOR
  //   000 Addition
  //   001 Subtraction
  //   010 Decrement
  //   011 Negation
  //   100 Multiply by 4 (INCOMPLETE)
endmodule
