// Logisim project hw4part2.circ as structural Verilog: 2 circuits, main circuit One-Hot State Machine
module Tester (
  input  G
);

  wire Clock_out, one_hot_state_machine_1_w, one_hot_state_machine_1_x, one_hot_state_machine_1_y,
       one_hot_state_machine_1_z, Reset_out;

  One_Hot_State_Machine one_hot_state_machine_1 (
    .W(one_hot_state_machine_1_w), .Clock(Clock_out), .Reset(Reset_out), .G(G),
    .X(one_hot_state_machine_1_x), .Y(one_hot_state_machine_1_y), .Z(one_hot_state_machine_1_z));
  Clock Clock (.out(Clock_out));
  LED W (.in(one_hot_state_machine_1_w));
  LED X (.in(one_hot_state_machine_1_x));
  LED Y (.in(one_hot_state_machine_1_y));
  LED Z (.in(one_hot_state_machine_1_z));
  Button Reset (.out(Reset_out));

  // Notes on the sheet:
  //   You can use this to test your circuit.
endmodule

module One_Hot_State_Machine (
  input  G,
  input  Clock,
  input  Reset,
  output W,
  output X,
  output Y,
  output Z
);

  wire and_3_out, and_4_out, and_5_out, and_7_out, and_8_out, and_9_out, and_10_out, and_11_out, and_12_out,
       D0, D2, D3, D4, D5, D6, G_prime, Q0, Q1, Q2, Q3, Q4, Q5, Q6;
  wire [6:0] nor_1_out;

  and and_1 (D0, G_prime, Q5);
  and and_2 (D2, G_prime, Q1);
  and and_3 (and_3_out, G_prime, Q2);
  and and_4 (and_4_out, G_prime, Q3);
  and and_5 (and_5_out, G, Q2);
  and and_6 (D4, G, Q1);
  and and_7 (and_7_out, G_prime, Q4);
  and and_8 (and_8_out, G, Q3);
  and and_9 (and_9_out, G, Q4);
  and and_10 (and_10_out, G_prime, Q5);
  and and_11 (and_11_out, G, Q5);
  and and_12 (and_12_out, G, Q6);
  or or_1 (D3, and_3_out, and_4_out, and_5_out);
  or or_2 (D5, and_7_out, and_8_out, and_9_out);
  or or_3 (D6, and_10_out, and_11_out, and_12_out);
  not not_1 (G_prime, G);
  assign nor_1_out = ~({D6, D5, D4, D3, D2, G, D0} | {Q6, Q5, Q4, Q3, Q2, Q1, Q0});  // NOR_Gate nor_1, 7 bits wide
  Register #(.width(7)) register_1 (
    .D(nor_1_out), .Q({Q6, Q5, Q4, Q3, Q2, Q1, Q0}), .clk(Clock), .clr(Reset));  // open: en
  or or_4 (W, Q2, Q3, Q6);
  or or_5 (X, Q0, Q3);
  or or_6 (Y, Q3, Q5, Q6);
  or or_7 (Z, Q2, Q4, Q5);

  // Other names for the same wires on the sheet: D1 = G; CLK = Clock; RST = Reset

  // Notes on the sheet:
  //   My name is
  //   Jesse Chen
  //   and this is my pretty one-hot state machine!
endmodule
